// Logisim project banco_de_registradores.circ as structural Verilog: 3 circuits, main circuit banco_de_registradores
module banco_de_registradores (
  input  CLK,
  input  EW,
  input  [31:0] WD,
  input  [4:0] LR1,
  input  [4:0] LR2,
  input  [4:0] WR,
  output [31:0] LD1,
  output [31:0] LD2
);

  wire _1_W, _2_W, _3_W, _4_W, _5_W, _6_W, _7_W, _8_W, _9_W, _10_W, _11_W, _12_W, _13_W, _14_W, _15_W, _16_W,
       _17_W, _18_W, _19_W, _20_W, _21_W, _22_W, _23_W, _24_W, _25_W, _26_W, _27_W, _28_W, _29_W, _30_W,
       _31_W, and_1_out, and_2_out, and_3_out, and_4_out, and_5_out, and_6_out, and_7_out, and_8_out,
       and_9_out, and_10_out, and_11_out, and_12_out, and_13_out, and_14_out, and_15_out, and_16_out,
       and_17_out, and_18_out, and_19_out, and_20_out, and_21_out, and_22_out, and_23_out, and_24_out,
       and_25_out, and_26_out, and_27_out, and_28_out, and_29_out, and_30_out, and_31_out;
  wire [31:0] _1_R, _2_R, _3_R, _4_R, _5_R, _6_R, _7_R, _8_R, _9_R, _10_R, _11_R, _12_R, _13_R, _14_R, _15_R,
       _16_R, _17_R, _18_R, _19_R, _20_R, _21_R, _22_R, _23_R, _24_R, _25_R, _26_R, _27_R, _28_R, _29_R,
       _30_R, _31_R;

  inverted_selector inverted_selector_1 (
    .OUTPUT(LD1), .SELECTOR(LR1), ._0({32{1'b0}}), ._1(_1_R), ._2(_2_R), ._3(_3_R), ._4(_4_R), ._5(_5_R),
    ._6(_6_R), ._7(_7_R), ._8(_8_R), ._9(_9_R), ._10(_10_R), ._11(_11_R), ._12(_12_R), ._13(_13_R),
    ._14(_14_R), ._15(_15_R), ._16(_16_R), ._17(_17_R), ._18(_18_R), ._19(_19_R), ._20(_20_R), ._21(_21_R),
    ._22(_22_R), ._23(_23_R), ._24(_24_R), ._25(_25_R), ._26(_26_R), ._27(_27_R), ._28(_28_R), ._29(_29_R),
    ._30(_30_R), ._31(_31_R));
  inverted_selector inverted_selector_2 (
    .OUTPUT(LD2), .SELECTOR(LR2), ._0({32{1'b0}}), ._1(_1_R), ._2(_2_R), ._3(_3_R), ._4(_4_R), ._5(_5_R),
    ._6(_6_R), ._7(_7_R), ._8(_8_R), ._9(_9_R), ._10(_10_R), ._11(_11_R), ._12(_12_R), ._13(_13_R),
    ._14(_14_R), ._15(_15_R), ._16(_16_R), ._17(_17_R), ._18(_18_R), ._19(_19_R), ._20(_20_R), ._21(_21_R),
    ._22(_22_R), ._23(_23_R), ._24(_24_R), ._25(_25_R), ._26(_26_R), ._27(_27_R), ._28(_28_R), ._29(_29_R),
    ._30(_30_R), ._31(_31_R));
  selector selector_1 (
    .INPUT(WR), ._31(_31_W), ._30(_30_W), ._29(_29_W), ._28(_28_W), ._27(_27_W), ._26(_26_W), ._25(_25_W),
    ._24(_24_W), ._23(_23_W), ._22(_22_W), ._21(_21_W), ._20(_20_W), ._19(_19_W), ._18(_18_W), ._17(_17_W),
    ._16(_16_W), ._15(_15_W), ._14(_14_W), ._13(_13_W), ._12(_12_W), ._11(_11_W), ._10(_10_W), ._9(_9_W),
    ._8(_8_W), ._7(_7_W), ._6(_6_W), ._5(_5_W), ._4(_4_W), ._3(_3_W), ._2(_2_W), ._1(_1_W));  // open: _0
  Register #(.width(32)) register_1 (.D(WD), .en(and_1_out), .Q(_8_R), .clk(CLK));  // open: clr
  and and_1 (and_1_out, _8_W, EW);
  Register #(.width(32)) register_2 (.D(WD), .en(and_2_out), .Q(_16_R), .clk(CLK));  // open: clr
  and and_2 (and_2_out, _16_W, EW);
  Register #(.width(32)) register_3 (.D(WD), .en(and_3_out), .Q(_24_R), .clk(CLK));  // open: clr
  and and_3 (and_3_out, _24_W, EW);
  and and_4 (and_4_out, _1_W, EW);
  and and_5 (and_5_out, _9_W, EW);
  and and_6 (and_6_out, _17_W, EW);
  and and_7 (and_7_out, _25_W, EW);
  Register #(.width(32)) register_4 (.D(WD), .en(and_4_out), .Q(_1_R), .clk(CLK));  // open: clr
  Register #(.width(32)) register_5 (.D(WD), .en(and_5_out), .Q(_9_R), .clk(CLK));  // open: clr
  Register #(.width(32)) register_6 (.D(WD), .en(and_6_out), .Q(_17_R), .clk(CLK));  // open: clr
  Register #(.width(32)) register_7 (.D(WD), .en(and_7_out), .Q(_25_R), .clk(CLK));  // open: clr
  and and_8 (and_8_out, _2_W, EW);
  and and_9 (and_9_out, _10_W, EW);
  and and_10 (and_10_out, _18_W, EW);
  and and_11 (and_11_out, _26_W, EW);
  Register #(.width(32)) register_8 (.D(WD), .en(and_8_out), .Q(_2_R), .clk(CLK));  // open: clr
  Register #(.width(32)) register_9 (.D(WD), .en(and_9_out), .Q(_10_R), .clk(CLK));  // open: clr
  Register #(.width(32)) register_10 (.D(WD), .en(and_10_out), .Q(_18_R), .clk(CLK));  // open: clr
  Register #(.width(32)) register_11 (.D(WD), .en(and_11_out), .Q(_26_R), .clk(CLK));  // open: clr
  and and_12 (and_12_out, _3_W, EW);
  and and_13 (and_13_out, _11_W, EW);
  and and_14 (and_14_out, _19_W, EW);
  and and_15 (and_15_out, _27_W, EW);
  Register #(.width(32)) register_12 (.D(WD), .en(and_12_out), .Q(_3_R), .clk(CLK));  // open: clr
  Register #(.width(32)) register_13 (.D(WD), .en(and_13_out), .Q(_11_R), .clk(CLK));  // open: clr
  Register #(.width(32)) register_14 (.D(WD), .en(and_14_out), .Q(_19_R), .clk(CLK));  // open: clr
  Register #(.width(32)) register_15 (.D(WD), .en(and_15_out), .Q(_27_R), .clk(CLK));  // open: clr
  Register #(.width(32)) register_16 (.D(WD), .en(and_16_out), .Q(_4_R), .clk(CLK));  // open: clr
  and and_16 (and_16_out, _4_W, EW);
  Register #(.width(32)) register_17 (.D(WD), .en(and_17_out), .Q(_12_R), .clk(CLK));  // open: clr
  and and_17 (and_17_out, _12_W, EW);
  and and_18 (and_18_out, _20_W, EW);
  and and_19 (and_19_out, _28_W, EW);
  Register #(.width(32)) register_18 (.D(WD), .en(and_18_out), .Q(_20_R), .clk(CLK));  // open: clr
  Register #(.width(32)) register_19 (.D(WD), .en(and_19_out), .Q(_28_R), .clk(CLK));  // open: clr
  and and_20 (and_20_out, _5_W, EW);
  Register #(.width(32)) register_20 (.D(WD), .en(and_20_out), .Q(_5_R), .clk(CLK));  // open: clr
  Register #(.width(32)) register_21 (.D(WD), .en(and_21_out), .Q(_13_R), .clk(CLK));  // open: clr
  and and_21 (and_21_out, _13_W, EW);
  Register #(.width(32)) register_22 (.D(WD), .en(and_22_out), .Q(_21_R), .clk(CLK));  // open: clr
  and and_22 (and_22_out, _21_W, EW);
  Register #(.width(32)) register_23 (.D(WD), .en(and_23_out), .Q(_29_R), .clk(CLK));  // open: clr
  and and_23 (and_23_out, _29_W, EW);
  and and_24 (and_24_out, _6_W, EW);
  and and_25 (and_25_out, _14_W, EW);
  Register #(.width(32)) register_24 (.D(WD), .en(and_24_out), .Q(_6_R), .clk(CLK));  // open: clr
  Register #(.width(32)) register_25 (.D(WD), .en(and_25_out), .Q(_14_R), .clk(CLK));  // open: clr
  Register #(.width(32)) register_26 (.D(WD), .en(and_26_out), .Q(_22_R), .clk(CLK));  // open: clr
  and and_26 (and_26_out, _22_W, EW);
  Register #(.width(32)) register_27 (.D(WD), .en(and_27_out), .Q(_30_R), .clk(CLK));  // open: clr
  and and_27 (and_27_out, _30_W, EW);
  and and_28 (and_28_out, _7_W, EW);
  and and_29 (and_29_out, _15_W, EW);
  and and_30 (and_30_out, _23_W, EW);
  and and_31 (and_31_out, _31_W, EW);
  Register #(.width(32)) register_28 (.D(WD), .en(and_28_out), .Q(_7_R), .clk(CLK));  // open: clr
  Register #(.width(32)) register_29 (.D(WD), .en(and_29_out), .Q(_15_R), .clk(CLK));  // open: clr
  Register #(.width(32)) register_30 (.D(WD), .en(and_30_out), .Q(_23_R), .clk(CLK));  // open: clr
  Register #(.width(32)) register_31 (.D(WD), .en(and_31_out), .Q(_31_R), .clk(CLK));  // open: clr
endmodule

module selector (
  input  [4:0] INPUT,
  output _31,
  output _30,
  output _29,
  output _28,
  output _27,
  output _26,
  output _25,
  output _24,
  output _23,
  output _22,
  output _21,
  output _20,
  output _19,
  output _18,
  output _17,
  output _16,
  output _15,
  output _14,
  output _13,
  output _12,
  output _11,
  output _10,
  output _9,
  output _8,
  output _7,
  output _6,
  output _5,
  output _4,
  output _3,
  output _2,
  output _1,
  output _0
);

  Demultiplexer #(.select(5)) demultiplexer_1 (
    .out0(_0), .out1(_1), .out2(_2), .out3(_3), .out4(_4), .out5(_5), .out6(_6), .out7(_7), .out8(_8),
    .out9(_9), .out10(_10), .out11(_11), .out12(_12), .out13(_13), .out14(_14), .out15(_15), .out16(_16),
    .out17(_17), .out18(_18), .out19(_19), .out20(_20), .out21(_21), .out22(_22), .out23(_23), .out24(_24),
    .out25(_25), .out26(_26), .out27(_27), .out28(_28), .out29(_29), .out30(_30), .out31(_31), .in(1'b1),
    .sel(INPUT));  // open: en
endmodule

module inverted_selector (
  input  [4:0] SELECTOR,
  input  [31:0] _0,
  input  [31:0] _1,
  input  [31:0] _2,
  input  [31:0] _3,
  input  [31:0] _4,
  input  [31:0] _5,
  input  [31:0] _6,
  input  [31:0] _7,
  input  [31:0] _8,
  input  [31:0] _9,
  input  [31:0] _10,
  input  [31:0] _11,
  input  [31:0] _12,
  input  [31:0] _13,
  input  [31:0] _14,
  input  [31:0] _15,
  input  [31:0] _16,
  input  [31:0] _17,
  input  [31:0] _18,
  input  [31:0] _19,
  input  [31:0] _20,
  input  [31:0] _21,
  input  [31:0] _22,
  input  [31:0] _23,
  input  [31:0] _24,
  input  [31:0] _25,
  input  [31:0] _26,
  input  [31:0] _27,
  input  [31:0] _28,
  input  [31:0] _29,
  input  [31:0] _30,
  input  [31:0] _31,
  output [31:0] OUTPUT
);

  wire [31:0] undriven;

  Multiplexer #(.select(5), .width(32)) multiplexer_1 (
    .in0(_0), .in1(_1), .in2(_2), .in3(_3), .in4(_4), .in5(_5), .in6(_6), .in7(_7), .in8(_8), .in9(_9),
    .in10(_10), .in11(_11), .in12(_12), .in13(_13), .in14(_14), .in15(_15), .in16(_16), .in17(undriven),
    .in18(_18), .in19(_19), .in20(_20), .in21(_21), .in22(_22), .in23(_23), .in24(_24), .in25(_25),
    .in26(_26), .in27(_27), .in28(_28), .in29(_29), .in30(_30), .in31(_31), .out(OUTPUT), .sel(SELECTOR));  // open: en
endmodule
