// Logisim project contole_excecao.circ as structural Verilog: 1 circuit, main circuit main
module main (
  input  CLK,
  input  WriteRes,
  input  except,
  input  [31:0] EPC_in,
  input  [4:0] WR_in,
  input  [31:0] res_data,
  output [31:0] EPC,
  output [4:0] WR_out,
  output [31:0] MFC0_out
);

  wire or_1_out;

  Register #(.width(32)) register_1 (.D(EPC_in), .en(except), .Q(EPC), .clk(CLK));  // open: clr
  Register #(.width(5)) register_2 (.D(WR_in), .en(except), .Q(WR_out), .clk(CLK));  // open: clr
  Register #(.width(32)) register_3 (.D(res_data), .en(or_1_out), .Q(MFC0_out), .clk(CLK));  // open: clr
  or or_1 (or_1_out, WriteRes, except);

  // Other names for the same wires on the sheet: EXPT = except; WR = WriteRes
endmodule
