// Logisim project decodificador_de_instrução.circ as structural Verilog: 2 circuits, main circuit decodificador_de_instrução
module \decodificador_de_instrução  (
  input  [31:0] \Instrução ,
  output [5:0] opcode,
  output [4:0] RS,
  output [4:0] RT,
  output [4:0] RD,
  output [4:0] shamt,
  output [5:0] funct,
  output [15:0] imm,
  output [25:0] addr
);

  wire ADDI_out, BEQ_out, BNE_out, J_out, JAL_out, LW_out, OP_I, OP_J, OP_R, SW_out;
  wire [4:0] multiplexer_1_out, multiplexer_2_out;
  wire [25:0] demultiplexer_1_out0, demultiplexer_2_out0;
  wire [25:16] I_INTRUCAO_SEM_OP, R_INTRUCAO_SEM_OP;

  Demultiplexer #(.width(26)) demultiplexer_1 (
    .out0(demultiplexer_1_out0), .out1(addr), .in(demultiplexer_2_out0), .sel(OP_J));  // open: en
  Demultiplexer #(.width(26)) demultiplexer_2 (
    .out0(demultiplexer_2_out0), .out1({R_INTRUCAO_SEM_OP, RD, shamt, funct}), .in(\Instrução [25:0]),
    .sel(OP_R));  // open: en
  and R (OP_R, ~\Instrução [31], ~\Instrução [30], ~\Instrução [29], ~\Instrução [28], ~\Instrução [27], ~\Instrução [26]);  // AND_Gate
  Demultiplexer #(.width(26)) demultiplexer_3 (
    .out1({I_INTRUCAO_SEM_OP, imm}), .in(demultiplexer_1_out0), .sel(OP_I));  // open: out0, en
  and J (J_out, ~\Instrução [31], ~\Instrução [30], ~\Instrução [29], ~\Instrução [28], \Instrução [27], ~\Instrução [26]);  // AND_Gate
  and JAL (JAL_out, ~\Instrução [31], ~\Instrução [30], ~\Instrução [29], ~\Instrução [28], \Instrução [27], \Instrução [26]);  // AND_Gate
  or or_1 (OP_J, J_out, JAL_out);
  and ADDI (ADDI_out, ~\Instrução [31], ~\Instrução [30], \Instrução [29], ~\Instrução [28], ~\Instrução [27], ~\Instrução [26]);  // AND_Gate
  Multiplexer #(.width(5)) multiplexer_1 (
    .in0({5{1'b0}}), .in1(R_INTRUCAO_SEM_OP[25:21]), .out(multiplexer_1_out), .sel(OP_R));  // open: en
  Multiplexer #(.width(5)) multiplexer_2 (
    .in0({5{1'b0}}), .in1(R_INTRUCAO_SEM_OP[20:16]), .out(multiplexer_2_out), .sel(OP_R));  // open: en
  and LW (LW_out, \Instrução [31], ~\Instrução [30], ~\Instrução [29], ~\Instrução [28], \Instrução [27], \Instrução [26]);  // AND_Gate
  Multiplexer #(.width(5)) multiplexer_3 (
    .in0(multiplexer_1_out), .in1(I_INTRUCAO_SEM_OP[25:21]), .out(RS), .sel(OP_I));  // open: en
  Multiplexer #(.width(5)) multiplexer_4 (
    .in0(multiplexer_2_out), .in1(I_INTRUCAO_SEM_OP[20:16]), .out(RT), .sel(OP_I));  // open: en
  and SW (SW_out, \Instrução [31], ~\Instrução [30], \Instrução [29], ~\Instrução [28], \Instrução [27], \Instrução [26]);  // AND_Gate
  or or_2 (OP_I, ADDI_out, LW_out, SW_out, BEQ_out, BNE_out);
  and BEQ (BEQ_out, ~\Instrução [31], ~\Instrução [30], ~\Instrução [29], \Instrução [28], ~\Instrução [27], ~\Instrução [26]);  // AND_Gate
  and BNE (BNE_out, ~\Instrução [31], ~\Instrução [30], ~\Instrução [29], \Instrução [28], ~\Instrução [27], \Instrução [26]);  // AND_Gate

  assign opcode = \Instrução [31:26];

  // Other names for the same wires on the sheet: I_imm[15:0] = imm; I_INTRUCAO_SEM_OP[15:0] = imm;
  //   I_RS[4:0] = I_INTRUCAO_SEM_OP[25:21]; I_RT[4:0] = I_INTRUCAO_SEM_OP[20:16]; J_addr[25:0] = addr;
  //   J_INTRUCAO_SEM_OP[25:0] = addr; R_FUNC[5:0] = funct; R_INTRUCAO_SEM_OP[15:0] = {RD, shamt, funct};
  //   R_RD[4:0] = RD; R_RS[4:0] = R_INTRUCAO_SEM_OP[25:21]; R_RT[4:0] = R_INTRUCAO_SEM_OP[20:16]; R_SH[4:0] = shamt
endmodule

module main (
);

  \decodificador_de_instrução  \decodificador_de_instrução_1  ();  // open: Instrução, opcode, RS, RT, RD, shamt, funct, imm, addr
endmodule
