// Logisim project Decodificador_Opcode.circ as structural Verilog: 2 circuits, main circuit main
module main (
);

  Decodificador_Opcode decodificador_opcode_1 ();  // open: R, J, I, RFE, MTC0, MFC0, Opcode
endmodule

module Decodificador_Opcode (
  input  [5:0] Opcode,
  output R,
  output J,
  output I,
  output RFE,
  output MTC0,
  output MFC0
);

  wire ADDI_out, BEQ_out, BNE_out, J_out, JAL_out, LW_out, SW_out;

  and u_R (R, ~Opcode[0], ~Opcode[1], ~Opcode[2], ~Opcode[3], ~Opcode[4], ~Opcode[5]);  // AND_Gate
  and u_J (J_out, ~Opcode[0], ~Opcode[1], ~Opcode[2], ~Opcode[3], Opcode[4], ~Opcode[5]);  // AND_Gate
  and JAL (JAL_out, ~Opcode[0], ~Opcode[1], ~Opcode[2], ~Opcode[3], Opcode[4], Opcode[5]);  // AND_Gate
  and ADDI (ADDI_out, ~Opcode[0], ~Opcode[1], Opcode[2], ~Opcode[3], ~Opcode[4], ~Opcode[5]);  // AND_Gate
  and LW (LW_out, Opcode[0], ~Opcode[1], ~Opcode[2], ~Opcode[3], Opcode[4], Opcode[5]);  // AND_Gate
  and SW (SW_out, Opcode[0], ~Opcode[1], Opcode[2], ~Opcode[3], Opcode[4], Opcode[5]);  // AND_Gate
  and BEQ (BEQ_out, ~Opcode[0], ~Opcode[1], ~Opcode[2], Opcode[3], ~Opcode[4], ~Opcode[5]);  // AND_Gate
  and BNE (BNE_out, ~Opcode[0], ~Opcode[1], ~Opcode[2], Opcode[3], ~Opcode[4], Opcode[5]);  // AND_Gate
  and u_RFE (RFE, Opcode[0], ~Opcode[1], ~Opcode[2], ~Opcode[3], ~Opcode[4], ~Opcode[5]);  // AND_Gate
  and u_MTC0 (MTC0, ~Opcode[0], Opcode[1], ~Opcode[2], ~Opcode[3], ~Opcode[4], ~Opcode[5]);  // AND_Gate
  and u_MFC0 (MFC0, Opcode[0], Opcode[1], ~Opcode[2], ~Opcode[3], ~Opcode[4], ~Opcode[5]);  // AND_Gate
  or or_1 (J, J_out, JAL_out);
  or or_2 (I, ADDI_out, LW_out, SW_out, BEQ_out, BNE_out);
endmodule
