// Logisim project MIPS.circ as structural Verilog: 2 circuits, main circuit main
module main (
  input  in_1
);

  wire ALUSrc, and_1_out, BNE, Branch, Clock, E_JR, exception, ExcOut, Jump, JumpRegister, Link, MemRead,
       MemtoReg, MemWrite, MTC0, multiplexer_4_out, not_1_out, or_1_out, RegDst, ula_1_overflow, ula_1_zero,
       unidade_de_controle_principal_1_regdst, unidade_de_controle_principal_1_writereg, WriteReg, Zero;
  wire [1:0] ALUOp;
  wire [3:0] Op;
  wire [4:0] multiplexer_8_out, multiplexer_9_out, rd, rs, rt, shamt, WR, WR_expect;
  wire [5:0] funct, opcode;
  wire [15:0] imm16;
  wire [25:0] addr;
  wire [31:0] adder_1_out, conc_1_result, EPC, imm32, LD, LD1, LD2, mem_instr_1_output, mfc0R,
       multiplexer_1_out, multiplexer_2_out, multiplexer_3_out, multiplexer_5_out, multiplexer_6_out,
       multiplexer_7_out, multiplexer_10_out, multiplexer_13_out, multiplexer_14_out, PC_4, PC_q, result, WD;

  Multiplexer #(.width(32), .enable("false")) multiplexer_1 (
    .in0(multiplexer_2_out), .in1(conc_1_result), .out(multiplexer_1_out), .sel(Jump));
  // Probe on multiplexer_1_out
  Multiplexer #(.width(32), .enable("false")) multiplexer_2 (
    .in0(multiplexer_7_out), .in1(LD1), .out(multiplexer_2_out), .sel(JumpRegister));
  not not_1 (not_1_out, Zero);
  Multiplexer #(.width(32), .enable("false")) multiplexer_3 (
    .in0(multiplexer_1_out), .in1(32'h2000000), .out(multiplexer_3_out), .sel(exception));
  // Probe on multiplexer_3_out
  // Probe on multiplexer_7_out
  Multiplexer #(.enable("false")) multiplexer_4 (.in0(Zero), .in1(not_1_out), .out(multiplexer_4_out), .sel(BNE));
  Multiplexer #(.width(32), .enable("false")) multiplexer_5 (
    .in0(multiplexer_3_out), .in1(EPC), .out(multiplexer_5_out), .sel(ExcOut));
  Multiplexer #(.width(32), .enable("false")) multiplexer_6 (
    .in0(result), .in1(LD1), .out(multiplexer_6_out), .sel(MTC0));
  Multiplexer #(.width(32), .enable("false")) multiplexer_7 (
    .in0(PC_4), .in1(adder_1_out), .out(multiplexer_7_out), .sel(and_1_out));
  and and_1 (and_1_out, multiplexer_4_out, Branch);
  // Probe on multiplexer_5_out
  // Probe on conc_1_result
  // Probe on multiplexer_6_out
  Clock clock_1 (.out(Clock));
  Register #(.width(32)) PC (.D(multiplexer_5_out), .en(1'b1), .Q(PC_q), .clk(Clock), .clr(in_1));
  or or_1 (or_1_out, MTC0, exception);
  Adder #(.width(32)) adder_1 (.a({imm32[29:0], 2'b00}), .b(PC_4), .out(adder_1_out));  // open: cin, cout
  Adder #(.width(32)) adder_2 (.a(32'h4), .b(PC_q), .out(PC_4));  // open: cin, cout
  // Probe on PC_q
  contole_excecao_main main_1 (
    .CLK(Clock), .WriteRes(or_1_out), .except(exception), .EPC_in(PC_4), .WR_in(WR),
    .res_data(multiplexer_6_out), .EPC(EPC), .WR_out(WR_expect), .MFC0_out(mfc0R));
  // Probe on PC_4
  mem_instr mem_instr_1 (.INPUT(PC_q), .OUTPUT(mem_instr_1_output));
  conc conc_1 (.PC_4(PC_4), .Addr(addr), .result(conc_1_result));
  // Probe on Op
  // Probe on JumpRegister
  // Probe on opcode
  // Probe on rs
  // Probe on rt
  // Probe on rd
  // Probe on shamt
  // Probe on funct
  // Probe on imm16
  // Probe on addr
  // Probe on mem_instr_1_output
  // Probe on ALUOp
  // Probe on RegDst
  // Probe on WriteReg
  // Probe on ALUSrc
  // Probe on MemtoReg
  // Probe on MemRead
  // Probe on MemWrite
  // Probe on Branch
  // Probe on BNE
  // Probe on Jump
  // Probe on Link
  // Probe on ExcOut
  // Probe on MTC0
  \decodificador_de_instrução  \decodificador_de_instrução_1  (
    .\Instrução (mem_instr_1_output), .opcode(opcode), .RS(rs), .RT(rt), .RD(rd), .shamt(shamt),
    .funct(funct), .imm(imm16), .addr(addr));
  unidade_de_controle_principal unidade_de_controle_principal_1 (
    .RegDst(unidade_de_controle_principal_1_regdst), .WriteReg(unidade_de_controle_principal_1_writereg),
    .ALUSrc(ALUSrc), .ExcOut(ExcOut), .ALUOp(ALUOp), .Opcode(opcode), .WriteRegEx(MTC0), .MenToReg(MemtoReg),
    .MenRead(MemRead), .MenWrite(MemWrite), .Branch(Branch), .Bne(BNE), .Jump(Jump), .Link(Link));
  // Probe on LD1
  // Probe on LD2
  // Probe on Zero
  // Probe on result
  // Probe on exception
  // Probe on LD
  // Probe on mfc0R
  // Probe on EPC
  // Probe on WR_expect
  // Probe on WR
  // Probe on WD
  Multiplexer #(.width(5), .enable("false")) multiplexer_8 (.in0(rt), .in1(rd), .out(multiplexer_8_out), .sel(RegDst));
  and and_2 (WriteReg, unidade_de_controle_principal_1_writereg, ~E_JR);  // AND_Gate
  Multiplexer #(.width(5), .enable("false")) multiplexer_9 (
    .in0(multiplexer_8_out), .in1(WR_expect), .out(multiplexer_9_out), .sel(ExcOut));
  Multiplexer #(.width(32), .enable("false")) multiplexer_10 (
    .in0(multiplexer_13_out), .in1(mfc0R), .out(multiplexer_10_out), .sel(ExcOut));
  extensor extensor_1 (.INPUT(imm16), .OUTPUT(imm32));
  and and_3 (E_JR, ~funct[0], ~funct[1], ~funct[2], funct[3], ~funct[4], ~funct[5]);  // AND_Gate
  and and_4 (RegDst, unidade_de_controle_principal_1_regdst, ~E_JR);  // AND_Gate
  Multiplexer #(.width(5), .enable("false")) multiplexer_11 (
    .in0(multiplexer_9_out), .in1({5{1'b1}}), .out(WR), .sel(Link));
  Multiplexer #(.width(32), .enable("false")) multiplexer_12 (
    .in0(multiplexer_10_out), .in1(PC_4), .out(WD), .sel(Link));
  UC_ULA uc_ula_1 (.ALUOP(ALUOp), .funct(funct), .JumpRegister(JumpRegister), .Op(Op));
  banco_de_registradores banco_de_registradores_1 (
    .CLK(Clock), .EW(WriteReg), .WD(WD), .LR1(rs), .LR2(rt), .WR(WR), .LD1(LD1), .LD2(LD2));
  Multiplexer #(.width(32), .enable("false")) multiplexer_13 (
    .in0(result), .in1(LD), .out(multiplexer_13_out), .sel(MemtoReg));
  ULA ula_1 (
    .Result(result), .Overflow(ula_1_overflow), .Zero(ula_1_zero), .A(LD1), .B(multiplexer_14_out),
    .Shamt(shamt), .\Operação (Op));
  Multiplexer #(.width(32), .enable("false")) multiplexer_14 (
    .in0(LD2), .in1(imm32), .out(multiplexer_14_out), .sel(ALUSrc));
  Multiplexer multiplexer_15 (.in0(ula_1_zero), .in1(1'b0), .out(Zero), .sel(E_JR));  // open: en
  Multiplexer multiplexer_16 (.in0(ula_1_overflow), .in1(1'b0), .out(exception), .sel(E_JR));  // open: en
  mem_data mem_data_1 (.address(result), .\input (LD2), .str(MemRead), .ld(MemWrite), .clk(Clock), .\output (LD));

  // Other names for the same wires on the sheet: Clear = in_1
endmodule

module conc (
  input  [31:0] PC_4,
  input  [25:0] Addr,
  output [31:0] result
);


  assign result = {PC_4[31:28], Addr, 2'b00};
endmodule
