// Logisim project memoria_dados.circ as structural Verilog: 1 circuit, main circuit mem_data
module mem_data (
  input  [31:0] address,
  input  [31:0] \input ,
  input  str,
  input  ld,
  input  clk,
  output [31:0] \output 
);

  RAM #(.addrWidth(24), .dataWidth(32), .bus("separate")) ram_1 (
    .addr(address[26:3]), .din(\input ), .data(\output ), .str(str), .clk(clk), .ld(ld));  // open: sel, clr

  // Other names for the same wires on the sheet: Addr[23:0] = address[26:3]; Clock = clk; Data_inp[31:0] = \input ;
  //   Data_out[31:0] = \output ; Load = ld; Store = str
endmodule
