// Logisim project memoria_inst.circ as structural Verilog: 2 circuits, main circuit mem_instr
module mem_instr (
  input  [31:0] INPUT,
  output [31:0] OUTPUT
);

  ROM #(.addrWidth(24), .dataWidth(32)) rom_1 (.addr(INPUT[27:4]), .data(OUTPUT));  // open: sel

  // Notes on the sheet:
  //   contents of rom_1 (hex, n*v repeats v):
  //   0 11111111 22222222 33333333 44444444 55555555 66666666 77777777 88888888 99999999
endmodule

module test (
);

  mem_instr mem_instr_1 ();  // open: INPUT, OUTPUT
endmodule
