// Logisim project contole_excecao.circ as structural Verilog: 1 circuit, main circuit main
module main (
  input  CLK,
  input  WriteRes,
  input  except,
  input  [31:0] EPC_in,
  input  [4:0] WR_in,
  input  [31:0] res_data,
  output [31:0] EPC,
  output [4:0] WR_out,
  output [31:0] MFC0_out
);

  wire [4:0] register_2_q;
  wire [31:0] register_1_q, register_3_q;

  Register #(.width(32)) register_1 (.D(EPC_in), .Q(register_1_q), .clk(CLK));  // open: en, clr
  Register #(.width(5)) register_2 (.D(WR_in), .Q(register_2_q), .clk(CLK));  // open: en, clr
  Register #(.width(32)) register_3 (.D(res_data), .en(WriteRes), .Q(register_3_q), .clk(CLK));  // open: clr
  assign EPC = except ? register_1_q : 32'bz;  // Controlled_Buffer controlled_buffer_1
  assign WR_out = except ? register_2_q : 5'bz;  // Controlled_Buffer controlled_buffer_2
  assign MFC0_out = except ? register_3_q : 32'bz;  // Controlled_Buffer controlled_buffer_3

  // Other names for the same wires on the sheet: EXPT = except; WR = WriteRes
endmodule
