// Logisim project extensor.circ as structural Verilog: 1 circuit, main circuit extensor
module extensor (
  input  [15:0] INPUT,
  output [31:0] OUTPUT
);


  assign OUTPUT = {{17{INPUT[15]}}, INPUT[14:0]};
endmodule
