// Logisim project memoria_dados.circ as structural Verilog: 3 circuits, main circuit mem_data
module mem_data (
  input  [31:0] address,
  input  [31:0] \input ,
  input  str,
  input  ld,
  input  clk,
  output [31:0] \output 
);

  RAM #(.addrWidth(24), .dataWidth(32), .bus("separate")) ram_1 (
    .addr(address[26:3]), .din(\input ), .data(\output ), .str(str), .clk(clk), .ld(ld));  // open: sel, clr

  // Other names for the same wires on the sheet: Addr[23:0] = address[26:3]; Clock = clk; Data_inp[31:0] = \input ;
  //   Data_out[31:0] = \output ; Load = ld; Store = str
endmodule

module address (
  input  [31:0] address,
  output [23:0] LOW,
  output [23:0] HIGH,
  output BIT
);

  or or_1 (BIT, address[31], address[30], address[29], address[28], address[27], address[26], address[25], address[24]);

  assign HIGH = address[23:0];
  assign LOW = address[31:8];
endmodule

module mem_data2 (
  input  [31:0] address,
  input  [31:0] \input ,
  input  str,
  input  ld,
  input  clk,
  output [31:0] \output 
);

  wire not_1_out, RAM2;
  wire [23:0] Addr, Addr1, Addr2;

  address address_1 (.address(address), .BIT(RAM2), .LOW(Addr2), .HIGH(Addr));
  not not_1 (not_1_out, RAM2);
  RAM #(.addrWidth(24), .dataWidth(32), .bus("separate")) ram_1 (
    .addr(Addr1), .din(\input ), .data(\output ), .str(str), .sel(not_1_out), .clk(clk), .ld(ld));  // open: clr
  RAM #(.addrWidth(24), .dataWidth(32), .bus("separate")) ram_2 (
    .addr(Addr2), .din(\input ), .data(\output ), .str(str), .sel(RAM2), .clk(clk), .ld(ld));  // open: clr

  // Other names for the same wires on the sheet: Clock = clk; Data_inp[31:0] = \input ; Data_out[31:0] = \output ;
  //   Load = ld; Store = str
endmodule
