// Logisim project ULA.circ as structural Verilog: 2 circuits, main circuit main
module main (
);

  ULA ula_1 ();  // open: Result, Overflow, Zero, A, B, Shamt, Operação
endmodule

module ULA (
  input  [4:0] Shamt,
  input  [3:0] \Operação ,
  input  [31:0] A,
  input  [31:0] B,
  output [31:0] Result,
  output Overflow,
  output Zero
);

  wire xnor_1_out, xnor_2_out;
  wire [0:0] R_SLT;
  wire [31:0] R_ADD, R_AND, R_NOR, R_OR, R_SLL, R_SRL, R_SUB, R_XOR;

  assign R_AND = A & B;  // AND_Gate and_1, 32 bits wide
  assign R_OR = A | B;  // OR_Gate or_1, 32 bits wide
  assign R_NOR = ~(A | B);  // NOR_Gate nor_1, 32 bits wide
  assign R_XOR = A ^ B;  // XOR_Gate xor_1, 32 bits wide
  Comparator #(.width(32)) comparator_1 (.a(A), .b(B), .lt(R_SLT[0]));  // open: gt, eq
  Adder #(.width(32)) adder_1 (.a(A), .b(B), .out(R_ADD));  // open: cin, cout
  Subtractor #(.width(32)) subtractor_1 (.a(A), .b(B), .out(R_SUB));  // open: bin, bout
  Shifter #(.width(32)) shifter_1 (.in(A), .\dist (Shamt), .out(R_SLL));
  Shifter #(.width(32), .shift("lr")) shifter_2 (.in(A), .\dist (Shamt), .out(R_SRL));
  Multiplexer #(.select(4), .width(32)) multiplexer_1 (
    .in0(R_AND), .in1(R_OR), .in2(R_NOR), .in3(R_XOR), .in4({{31{1'b0}}, R_SLT[0]}), .in5(R_ADD),
    .in6(R_SUB), .in7(R_SLL), .in8(R_SRL), .out(Result), .sel(\Operação ));  // open: in9, in10, in11, in12, in13, in14, in15, en
  and and_2 (Zero, ~Result[0], ~Result[1], ~Result[2], ~Result[3], ~Result[4], ~Result[5], ~Result[6], ~Result[7], ~Result[8], ~Result[9], ~Result[10], ~Result[11], ~Result[12], ~Result[13], ~Result[14], ~Result[15], ~Result[17], ~Result[18], ~Result[19], ~Result[20], ~Result[21], ~Result[22], ~Result[23], ~Result[24], ~Result[25], ~Result[26], ~Result[27], ~Result[28], ~Result[29], ~Result[30], ~Result[31], ~Result[16]);  // AND_Gate
  NotExactlyOne xnor_1 (.out(xnor_1_out), .in0(A[31]), .in1(B[31]), .in2(Result[31]));
  NotExactlyOne xnor_2 (.out(xnor_2_out), .in0(A[31]), .in1(B[31]), .in2(Result[31]));
  Multiplexer #(.select(4)) multiplexer_2 (
    .in0(1'b0), .in1(1'b0), .in2(1'b0), .in3(1'b0), .in4(1'b0), .in5(xnor_1_out), .in6(xnor_2_out),
    .in7(1'b0), .in8(1'b0), .in9(1'b0), .in10(1'b0), .in11(1'b0), .in12(1'b0), .in13(1'b0), .in14(1'b0),
    .in15(1'b0), .out(Overflow), .sel(\Operação ));  // open: en

  // Other names for the same wires on the sheet: A_SINAL = A[31]; B_SINAL = B[31]; R_SINAL = Result[31]
endmodule
