// Logisim project Unidade_de_Controle_ULA.circ as structural Verilog: 3 circuits, main circuit UC_ULA
module UC_ULA (
  input  [1:0] ALUOP,
  input  [5:0] funct,
  output [3:0] Op
);

  wire nor_1_out;
  wire [3:0] func_translator_1_output;

  nor nor_1 (nor_1_out, ALUOP[0], ALUOP[1]);
  func_translator func_translator_1 (.\input (funct), .\output (func_translator_1_output));
  assign Op = nor_1_out ? func_translator_1_output : 4'bz;  // Controlled_Buffer controlled_buffer_1
endmodule

module func_translator (
  input  [5:0] \input ,
  output [3:0] \output 
);

  wire slt, ucula_comp_1_active, ucula_comp_2_active, ucula_comp_3_active, ucula_comp_4_active,
       ucula_comp_5_active, ucula_comp_6_active, ucula_comp_7_active, ucula_comp_8_active,
       ucula_comp_9_active;
  wire [3:0] op, ucula_comp_1_output, ucula_comp_2_output, ucula_comp_3_output, ucula_comp_4_output,
       ucula_comp_5_output, ucula_comp_6_output, ucula_comp_7_output, ucula_comp_8_output,
       ucula_comp_9_output;

  UCULA_comp ucula_comp_1 (
    .func_inp(\input ), .func_val(6'b100100), .op(4'b0000), .\output (ucula_comp_1_output),
    .active(ucula_comp_1_active));
  UCULA_comp ucula_comp_2 (
    .func_inp(\input ), .func_val(6'b100101), .op(4'b0001), .\output (ucula_comp_2_output),
    .active(ucula_comp_2_active));
  UCULA_comp ucula_comp_3 (
    .func_inp(\input ), .func_val(6'b100111), .op(4'b0010), .\output (ucula_comp_3_output),
    .active(ucula_comp_3_active));
  UCULA_comp ucula_comp_4 (
    .func_inp(\input ), .func_val(6'b100110), .op(4'b0011), .\output (ucula_comp_4_output),
    .active(ucula_comp_4_active));
  UCULA_comp ucula_comp_5 (
    .func_inp(\input ), .func_val(6'b100000), .op(4'b0101), .\output (ucula_comp_5_output),
    .active(ucula_comp_5_active));
  UCULA_comp ucula_comp_6 (
    .func_inp(\input ), .func_val(6'b100010), .op(4'b0110), .\output (ucula_comp_6_output),
    .active(ucula_comp_6_active));
  UCULA_comp ucula_comp_7 (
    .func_inp(\input ), .func_val(6'b101010), .op(4'b0100), .\output (ucula_comp_7_output),
    .active(ucula_comp_7_active));
  UCULA_comp ucula_comp_8 (
    .func_inp(\input ), .func_val({6{1'b0}}), .op(4'b0111), .\output (ucula_comp_8_output),
    .active(ucula_comp_8_active));
  UCULA_comp ucula_comp_9 (
    .func_inp(\input ), .func_val(6'b000010), .op(4'b1000), .\output (ucula_comp_9_output),
    .active(ucula_comp_9_active));
  assign op = ucula_comp_1_output | ucula_comp_2_output | ucula_comp_3_output | ucula_comp_4_output | ucula_comp_5_output | ucula_comp_6_output | ucula_comp_7_output | ucula_comp_8_output | ucula_comp_9_output;  // OR_Gate or_1, 4 bits wide
  or or_2 (slt, ucula_comp_1_active, ucula_comp_2_active, ucula_comp_3_active, ucula_comp_4_active, ucula_comp_5_active, ucula_comp_6_active, ucula_comp_7_active, ucula_comp_8_active, ucula_comp_9_active);
  assign \output  = slt ? op : 4'bz;  // Controlled_Buffer controlled_buffer_1
endmodule

module UCULA_comp (
  input  [5:0] func_inp,
  input  [5:0] func_val,
  input  [3:0] op,
  output [3:0] \output ,
  output active
);

  wire [5:0] xnor_1_out;

  assign xnor_1_out = ~(func_inp ^ func_val);  // XNOR_Gate xnor_1, 6 bits wide
  and and_1 (active, xnor_1_out[0], xnor_1_out[1], xnor_1_out[2], xnor_1_out[3], xnor_1_out[4], xnor_1_out[5]);
  assign \output  = op & {4{active}};  // AND_Gate and_2, 4 bits wide
endmodule
