// Logisim project Unidade_de_Controle_Principal.circ as structural Verilog: 2 circuits, main circuit main
module main (
);

  unidade_de_controle_principal unidade_de_controle_principal_1 ();  // open: RegDst, WriteReg, ALUSrc, ExcOut, ALUOp, Opcode, WriteRegEx, MenToReg, MenRead, MenWrite, Branch, Bne, Jump, Link
  unidade_de_controle_principal unidade_de_controle_principal_2 ();  // open: RegDst, WriteReg, ALUSrc, ExcOut, ALUOp, Opcode, WriteRegEx, MenToReg, MenRead, MenWrite, Branch, Bne, Jump, Link
  // Decodificador_Opcode decodificador_opcode_1: pin names not known
endmodule

module unidade_de_controle_principal (
  input  [5:0] Opcode,
  output [1:0] ALUOp,
  output RegDst,
  output WriteReg,
  output ALUSrc,
  output MenToReg,
  output MenRead,
  output MenWrite,
  output Branch,
  output Bne,
  output Jump,
  output Link,
  output ExcOut,
  output WriteRegEx
);

  wire decodificador_opcode_1_addi, decodificador_opcode_1_beq, decodificador_opcode_1_bne,
       decodificador_opcode_1_j, decodificador_opcode_1_jal, decodificador_opcode_1_lw,
       decodificador_opcode_1_mfc0, decodificador_opcode_1_mtc0, decodificador_opcode_1_r,
       decodificador_opcode_1_rfe, decodificador_opcode_1_sw;
  wire [13:0] multiplexer_1_out, multiplexer_2_out, multiplexer_3_out, multiplexer_4_out, multiplexer_5_out,
       multiplexer_6_out, multiplexer_7_out, multiplexer_8_out, multiplexer_9_out, multiplexer_10_out;

  Decodificador_Opcode decodificador_opcode_1 (
    .R(decodificador_opcode_1_r), .J(decodificador_opcode_1_j), .RFE(decodificador_opcode_1_rfe),
    .MTC0(decodificador_opcode_1_mtc0), .MFC0(decodificador_opcode_1_mfc0), .Opcode(Opcode),
    .JAL(decodificador_opcode_1_jal), .ADDi(decodificador_opcode_1_addi), .LW(decodificador_opcode_1_lw),
    .SW(decodificador_opcode_1_sw), .BEQ(decodificador_opcode_1_beq), .BNE(decodificador_opcode_1_bne));
  Multiplexer #(.width(14)) multiplexer_1 (
    .in0({14{1'b0}}), .in1(14'hc), .out(multiplexer_1_out), .sel(decodificador_opcode_1_r));  // open: en
  Multiplexer #(.width(14)) multiplexer_2 (
    .in0(multiplexer_1_out), .in1(14'h400), .out(multiplexer_2_out), .sel(decodificador_opcode_1_j));  // open: en
  Multiplexer #(.width(14)) multiplexer_3 (
    .in0(multiplexer_2_out), .in1(14'hc08), .out(multiplexer_3_out), .sel(decodificador_opcode_1_jal));  // open: en
  Multiplexer #(.width(14)) multiplexer_4 (
    .in0(multiplexer_3_out), .in1(14'h19), .out(multiplexer_4_out), .sel(decodificador_opcode_1_addi));  // open: en
  Multiplexer #(.width(14)) multiplexer_5 (
    .in0(multiplexer_4_out), .in1(14'h79), .out(multiplexer_5_out), .sel(decodificador_opcode_1_lw));  // open: en
  Multiplexer #(.width(14)) multiplexer_6 (
    .in0(multiplexer_5_out), .in1(14'h91), .out(multiplexer_6_out), .sel(decodificador_opcode_1_sw));  // open: en
  Multiplexer #(.width(14)) multiplexer_7 (
    .in0(multiplexer_6_out), .in1(14'h102), .out(multiplexer_7_out), .sel(decodificador_opcode_1_beq));  // open: en
  Multiplexer #(.width(14)) multiplexer_8 (
    .in0(multiplexer_7_out), .in1(14'h302), .out(multiplexer_8_out), .sel(decodificador_opcode_1_bne));  // open: en
  Multiplexer #(.width(14)) multiplexer_9 (
    .in0(multiplexer_8_out), .in1(14'h1008), .out(multiplexer_9_out), .sel(decodificador_opcode_1_rfe));  // open: en
  Multiplexer #(.width(14)) multiplexer_10 (
    .in0(multiplexer_9_out), .in1(14'h2000), .out(multiplexer_10_out), .sel(decodificador_opcode_1_mtc0));  // open: en
  Multiplexer #(.width(14)) multiplexer_11 (
    .in0(multiplexer_10_out), .in1(14'h8),
    .out({WriteRegEx, ExcOut, Link, Jump, Bne, Branch, MenWrite, MenRead, MenToReg, ALUSrc, WriteReg, RegDst, ALUOp}),
    .sel(decodificador_opcode_1_mfc0));  // open: en
endmodule
