// Logisim project memoria.circ as structural Verilog: 4 circuits, main circuit mem_cell
module mem_cell (
  input  [31:0] address,
  input  [31:0] data_in,
  input  [7:0] constant,
  input  clk,
  input  clr,
  input  ld,
  input  str,
  output [31:0] data_out
);

  wire comparator_1_eq, slct, xor_1_out;
  wire [31:0] extensor_1bit_1_out_2, ram_1_data;

  Comparator comparator_1 (.a(address[31:24]), .b(constant), .eq(comparator_1_eq));  // open: gt, lt
  xor xor_1 (xor_1_out, str, ld);
  and and_1 (slct, comparator_1_eq, xor_1_out);
  RAM #(.addrWidth(24), .dataWidth(32), .bus("separate")) ram_1 (
    .addr(address[23:0]), .din(data_in), .data(ram_1_data), .str(str), .sel(slct), .clk(clk), .ld(ld),
    .clr(clr));
  extensor_1bit extensor_1bit_1 (.in_1(slct), .out_2(extensor_1bit_1_out_2));
  assign data_out = ram_1_data & extensor_1bit_1_out_2;  // AND_Gate and_2, 32 bits wide

  // Other names for the same wires on the sheet: low[23:0] = address[23:0]; high[7:0] = address[31:24];
  //   din[31:0] = data_in
endmodule

module mem_bank (
  input  [31:0] address,
  input  [31:0] data_in,
  input  clk,
  input  clr,
  input  ld,
  input  str,
  input  [7:0] \const ,
  output [31:0] \output 
);

  wire [7:0] adder_1_out, adder_2_out, adder_3_out, adder_4_out, adder_5_out, adder_6_out, adder_7_out,
       adder_8_out, adder_9_out, adder_10_out, adder_11_out, adder_12_out, adder_13_out, adder_14_out,
       adder_15_out;
  wire [31:0] mem_cell_1_data_out, mem_cell_2_data_out, mem_cell_3_data_out, mem_cell_4_data_out,
       mem_cell_5_data_out, mem_cell_6_data_out, mem_cell_7_data_out, mem_cell_8_data_out,
       mem_cell_9_data_out, mem_cell_10_data_out, mem_cell_11_data_out, mem_cell_12_data_out,
       mem_cell_13_data_out, mem_cell_14_data_out, mem_cell_15_data_out, mem_cell_16_data_out, or_1_out,
       or_2_out, or_3_out, or_4_out;

  Adder adder_1 (.a(\const ), .b(8'h4), .out(adder_1_out));  // open: cin, cout
  Adder adder_2 (.a(\const ), .b(8'h8), .out(adder_2_out));  // open: cin, cout
  Adder adder_3 (.a(\const ), .b(8'hc), .out(adder_3_out));  // open: cin, cout
  mem_cell mem_cell_1 (
    .address(address), .data_in(data_in), .constant(\const ), .clk(clk), .clr(clr), .ld(ld), .str(str),
    .data_out(mem_cell_1_data_out));
  mem_cell mem_cell_2 (
    .address(address), .data_in(data_in), .constant(adder_1_out), .clk(clk), .clr(clr), .ld(ld), .str(str),
    .data_out(mem_cell_2_data_out));
  mem_cell mem_cell_3 (
    .address(address), .data_in(data_in), .constant(adder_2_out), .clk(clk), .clr(clr), .ld(ld), .str(str),
    .data_out(mem_cell_3_data_out));
  mem_cell mem_cell_4 (
    .address(address), .data_in(data_in), .constant(adder_3_out), .clk(clk), .clr(clr), .ld(ld), .str(str),
    .data_out(mem_cell_4_data_out));
  Adder adder_4 (.a(\const ), .b(8'h1), .out(adder_4_out));  // open: cin, cout
  Adder adder_5 (.a(\const ), .b(8'h5), .out(adder_5_out));  // open: cin, cout
  Adder adder_6 (.a(\const ), .b(8'h9), .out(adder_6_out));  // open: cin, cout
  Adder adder_7 (.a(\const ), .b(8'hd), .out(adder_7_out));  // open: cin, cout
  mem_cell mem_cell_5 (
    .address(address), .data_in(data_in), .constant(adder_4_out), .clk(clk), .clr(clr), .ld(ld), .str(str),
    .data_out(mem_cell_5_data_out));
  mem_cell mem_cell_6 (
    .address(address), .data_in(data_in), .constant(adder_5_out), .clk(clk), .clr(clr), .ld(ld), .str(str),
    .data_out(mem_cell_6_data_out));
  mem_cell mem_cell_7 (
    .address(address), .data_in(data_in), .constant(adder_6_out), .clk(clk), .clr(clr), .ld(ld), .str(str),
    .data_out(mem_cell_7_data_out));
  mem_cell mem_cell_8 (
    .address(address), .data_in(data_in), .constant(adder_7_out), .clk(clk), .clr(clr), .ld(ld), .str(str),
    .data_out(mem_cell_8_data_out));
  Adder adder_8 (.a(\const ), .b(8'h2), .out(adder_8_out));  // open: cin, cout
  Adder adder_9 (.a(\const ), .b(8'h6), .out(adder_9_out));  // open: cin, cout
  Adder adder_10 (.a(\const ), .b(8'ha), .out(adder_10_out));  // open: cin, cout
  Adder adder_11 (.a(\const ), .b(8'he), .out(adder_11_out));  // open: cin, cout
  mem_cell mem_cell_9 (
    .address(address), .data_in(data_in), .constant(adder_8_out), .clk(clk), .clr(clr), .ld(ld), .str(str),
    .data_out(mem_cell_9_data_out));
  mem_cell mem_cell_10 (
    .address(address), .data_in(data_in), .constant(adder_9_out), .clk(clk), .clr(clr), .ld(ld), .str(str),
    .data_out(mem_cell_10_data_out));
  mem_cell mem_cell_11 (
    .address(address), .data_in(data_in), .constant(adder_10_out), .clk(clk), .clr(clr), .ld(ld), .str(str),
    .data_out(mem_cell_11_data_out));
  mem_cell mem_cell_12 (
    .address(address), .data_in(data_in), .constant(adder_11_out), .clk(clk), .clr(clr), .ld(ld), .str(str),
    .data_out(mem_cell_12_data_out));
  Adder adder_12 (.a(\const ), .b(8'h3), .out(adder_12_out));  // open: cin, cout
  Adder adder_13 (.a(\const ), .b(8'h7), .out(adder_13_out));  // open: cin, cout
  Adder adder_14 (.a(\const ), .b(8'hb), .out(adder_14_out));  // open: cin, cout
  Adder adder_15 (.a(\const ), .b(8'hf), .out(adder_15_out));  // open: cin, cout
  mem_cell mem_cell_13 (
    .address(address), .data_in(data_in), .constant(adder_12_out), .clk(clk), .clr(clr), .ld(ld), .str(str),
    .data_out(mem_cell_13_data_out));
  mem_cell mem_cell_14 (
    .address(address), .data_in(data_in), .constant(adder_13_out), .clk(clk), .clr(clr), .ld(ld), .str(str),
    .data_out(mem_cell_14_data_out));
  mem_cell mem_cell_15 (
    .address(address), .data_in(data_in), .constant(adder_14_out), .clk(clk), .clr(clr), .ld(ld), .str(str),
    .data_out(mem_cell_15_data_out));
  mem_cell mem_cell_16 (
    .address(address), .data_in(data_in), .constant(adder_15_out), .clk(clk), .clr(clr), .ld(ld), .str(str),
    .data_out(mem_cell_16_data_out));
  assign or_1_out = mem_cell_13_data_out | mem_cell_9_data_out | mem_cell_5_data_out | mem_cell_1_data_out;  // OR_Gate or_1, 32 bits wide
  assign or_2_out = mem_cell_14_data_out | mem_cell_10_data_out | mem_cell_6_data_out | mem_cell_2_data_out;  // OR_Gate or_2, 32 bits wide
  assign or_3_out = mem_cell_15_data_out | mem_cell_11_data_out | mem_cell_7_data_out | mem_cell_3_data_out;  // OR_Gate or_3, 32 bits wide
  assign or_4_out = mem_cell_16_data_out | mem_cell_12_data_out | mem_cell_8_data_out | mem_cell_4_data_out;  // OR_Gate or_4, 32 bits wide
  assign \output  = or_1_out | or_2_out | or_3_out | or_4_out;  // OR_Gate or_5, 32 bits wide

  // Other names for the same wires on the sheet: addr[31:0] = address; din[31:0] = data_in
endmodule

module mem_32_bits (
  input  [31:0] address,
  input  [31:0] data_in,
  input  clk,
  input  clr,
  input  ld,
  input  str,
  output [31:0] \output 
);

  wire [31:0] mem_bank_1_output, mem_bank_2_output, mem_bank_3_output, mem_bank_4_output, mem_bank_5_output,
       mem_bank_6_output, mem_bank_7_output, mem_bank_8_output, mem_bank_9_output, mem_bank_10_output,
       mem_bank_11_output, mem_bank_12_output, mem_bank_13_output, mem_bank_14_output, mem_bank_15_output,
       mem_bank_16_output, or_1_out, or_2_out, or_3_out, or_4_out;

  mem_bank mem_bank_1 (
    .address(address), .data_in(data_in), .clk(clk), .clr(clr), .ld(ld), .str(str), .\const ({8{1'b0}}),
    .\output (mem_bank_1_output));
  mem_bank mem_bank_2 (
    .address(address), .data_in(data_in), .clk(clk), .clr(clr), .ld(ld), .str(str), .\const (8'h40),
    .\output (mem_bank_2_output));
  mem_bank mem_bank_3 (
    .address(address), .data_in(data_in), .clk(clk), .clr(clr), .ld(ld), .str(str), .\const (8'h80),
    .\output (mem_bank_3_output));
  mem_bank mem_bank_4 (
    .address(address), .data_in(data_in), .clk(clk), .clr(clr), .ld(ld), .str(str), .\const (8'hc0),
    .\output (mem_bank_4_output));
  mem_bank mem_bank_5 (
    .address(address), .data_in(data_in), .clk(clk), .clr(clr), .ld(ld), .str(str), .\const (8'h10),
    .\output (mem_bank_5_output));
  mem_bank mem_bank_6 (
    .address(address), .data_in(data_in), .clk(clk), .clr(clr), .ld(ld), .str(str), .\const (8'h50),
    .\output (mem_bank_6_output));
  mem_bank mem_bank_7 (
    .address(address), .data_in(data_in), .clk(clk), .clr(clr), .ld(ld), .str(str), .\const (8'h90),
    .\output (mem_bank_7_output));
  mem_bank mem_bank_8 (
    .address(address), .data_in(data_in), .clk(clk), .clr(clr), .ld(ld), .str(str), .\const (8'hd0),
    .\output (mem_bank_8_output));
  mem_bank mem_bank_9 (
    .address(address), .data_in(data_in), .clk(clk), .clr(clr), .ld(ld), .str(str), .\const (8'h20),
    .\output (mem_bank_9_output));
  mem_bank mem_bank_10 (
    .address(address), .data_in(data_in), .clk(clk), .clr(clr), .ld(ld), .str(str), .\const (8'h60),
    .\output (mem_bank_10_output));
  mem_bank mem_bank_11 (
    .address(address), .data_in(data_in), .clk(clk), .clr(clr), .ld(ld), .str(str), .\const (8'ha0),
    .\output (mem_bank_11_output));
  mem_bank mem_bank_12 (
    .address(address), .data_in(data_in), .clk(clk), .clr(clr), .ld(ld), .str(str), .\const (8'he0),
    .\output (mem_bank_12_output));
  mem_bank mem_bank_13 (
    .address(address), .data_in(data_in), .clk(clk), .clr(clr), .ld(ld), .str(str), .\const (8'h30),
    .\output (mem_bank_13_output));
  mem_bank mem_bank_14 (
    .address(address), .data_in(data_in), .clk(clk), .clr(clr), .ld(ld), .str(str), .\const (8'h70),
    .\output (mem_bank_14_output));
  mem_bank mem_bank_15 (
    .address(address), .data_in(data_in), .clk(clk), .clr(clr), .ld(ld), .str(str), .\const (8'hb0),
    .\output (mem_bank_15_output));
  mem_bank mem_bank_16 (
    .address(address), .data_in(data_in), .clk(clk), .clr(clr), .ld(ld), .str(str), .\const (8'hf0),
    .\output (mem_bank_16_output));
  assign or_1_out = mem_bank_13_output | mem_bank_9_output | mem_bank_5_output | mem_bank_1_output;  // OR_Gate or_1, 32 bits wide
  assign or_2_out = mem_bank_14_output | mem_bank_10_output | mem_bank_6_output | mem_bank_2_output;  // OR_Gate or_2, 32 bits wide
  assign or_3_out = mem_bank_15_output | mem_bank_11_output | mem_bank_7_output | mem_bank_3_output;  // OR_Gate or_3, 32 bits wide
  assign or_4_out = mem_bank_16_output | mem_bank_12_output | mem_bank_8_output | mem_bank_4_output;  // OR_Gate or_4, 32 bits wide
  assign \output  = or_1_out | or_2_out | or_3_out | or_4_out;  // OR_Gate or_5, 32 bits wide

  // Other names for the same wires on the sheet: addr[31:0] = address; din[31:0] = data_in
endmodule

module extensor_1bit (
  input  in_1,
  output [31:0] out_2
);


  assign out_2 = {32{in_1}};
endmodule
